# Fritzing sketch CapstoneDesign_Sketch (saved by Fritzing 0.9.6b)
circuit board: 8.46667cm x 5.64444cm
breadboards: 1

parts:
  LED1 = LED - 5mm [color="Red (633nm)" current=0.030 package="5 mm [THT]"]
  LED2 = LED - 5mm [color="Red (633nm)" current=0.030 package="5 mm [THT]"]
  LED3 = LED - 5mm [color="Blue (430nm)" current=0.030 package="5 mm [THT]"]
  LED4 = LED - 5mm [color="Blue (430nm)" current=0.030 package="5 mm [THT]"]
  LCD1 = LCD screen
  R5 = Photocell (LDR) [package=THT]
  LCM1602_IIC1 = LCM1602 IIC [part_number="LCM1602 IIC" chip_label="LCM1602 IIC" package="DIP (Dual Inline) [THT]"]
  YL-83_-_Control_Board1 = YL-83 Rain Sensor - Control Board
  R2 = Resistor [tolerance=±5% power=0.25 resistance=220 package=THT]
  R6 = Resistor [tolerance=±5% power=0.25 resistance=220 package=THT]
  부품1 = Arduino Uno (Rev3)

nets:
  GND: LED1.cathode, LED2.cathode, LED3.cathode, LED4.cathode, LCM1602_IIC1.GND, YL-83_-_Control_Board1.GND, 부품1.GND
  N1: LED1.anode, LED2.anode
  N2: LED3.anode, LED4.anode, R2.Pin_1
  VSS: LCD1.VSS, LCM1602_IIC1.VSS
  VDD: LCD1.VDD, LCM1602_IIC1.VDD
  N3: LCD1.V0, LCM1602_IIC1.V0
  N4: LCD1.RS, LCM1602_IIC1.RS
  N5: LCD1.R/W, LCM1602_IIC1.RW
  N6: LCD1.E, LCM1602_IIC1.E
  N7: LCD1.DB0, LCM1602_IIC1.D0
  N8: LCD1.DB1, LCM1602_IIC1.D1
  N9: LCD1.DB2, LCM1602_IIC1.D2
  N10: LCD1.DB3, LCM1602_IIC1.D3
  N11: LCD1.DB4, LCM1602_IIC1.D4
  N12: LCD1.DB5, LCM1602_IIC1.D5
  N13: LCD1.DB6, LCM1602_IIC1.D6
  N14: LCD1.DB7, LCM1602_IIC1.D7
  N15: LCD1.LED+, LCM1602_IIC1.A
  N16: LCD1.LED-, LCM1602_IIC1.K
  N17: R5.pin_0, YL-83_-_Control_Board1.NEG
  N18: R5.pin_1, YL-83_-_Control_Board1.POS
  VCC: LCM1602_IIC1.VCC, YL-83_-_Control_Board1.VCC, 부품1.5V
  N19: LCM1602_IIC1.SDA, 부품1.A4/SDA
  N20: LCM1602_IIC1.SCL, 부품1.A5/SCL
  N21: YL-83_-_Control_Board1.AO, 부품1.A3
  N22: R2.Pin_0, 부품1.D4
  N23: R6.Pin_0, 부품1.D7

custom parts:
  LCM1602 IIC: I2C-Module to use a 1602 or 2004 LCD on with the wire.h libory Serial LCD Modul
  YL-83 Rain Sensor - Control Board: The YL-83 is a rain sensor that has more resistance when dry and less resistance when wet. The module runs at 5V.
